# Fritzing sketch Tora_Fritzing (saved by Fritzing 0.9.4)
breadboards: 1

parts:
  J1 = Basic Servo
  J2 = Basic Servo
  J3 = Basic Servo
  J4 = Basic Servo
  J5 = Piezo Speaker
  Part1 = Adafruit 1.44 inch TFT Breakout [part_number="Adafruit #2088"]
  HC-SR04_Sensor_1 = HC-SR04 Ultrasonic Distance Sensor
  Part2 = Adafruit ItsyBitsy M4 [part_number="Adafruit #3800"]
  R1 = Resistor [tolerance=±5% resistance=220 package="0603 [SMD]"]
  R2 = Resistor [tolerance=±5% resistance=220 package="0603 [SMD]"]

nets:
  GND: J1.gnd, J2.gnd, J3.gnd, J4.gnd
  VCC: J1.vcc, J2.vcc, J3.vcc, J4.vcc, Part1.VIN, HC-SR04_Sensor_1.VCC, Part2.VBUS
  N1: J1.pulse, Part2.D11
  N2: J2.pulse, Part2.D12
  N3: J3.pulse, Part2.D9
  N4: J4.pulse, Part2.D10
  GND_2: J5.pin1, Part1.GND, HC-SR04_Sensor_1.GND, Part2.GND, R1.Pin_0
  N5: J5.pin2, Part2.D5_5V
  N6: Part1.SCK, Part2.SCK
  N7: Part1.MISO, Part2.MISO
  N8: Part1.TFTCS, Part2.D3
  N9: Part1.RESET, Part2.D7
  N10: HC-SR04_Sensor_1.TRIG, Part2.A0
  N11: HC-SR04_Sensor_1.ECHO, R2.Pin_1
  N12: Part2.A2, R1.Pin_1, R2.Pin_0

custom parts:
  Adafruit 1.44 inch TFT Breakout: This lovely little display breakout is the best way to add a small, colorful and bright display to any project. Since the display uses 4-wire SPI to communicate and has its own pixel-addressable frame buffer, it can be used with every kind of microcontroller. Even a very small one with low memory and few pins available! The 1.44" display has 128x128 color pixels. Unlike the low cost "Nokia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
  Adafruit ItsyBitsy M4: What's smaller than a Feather but larger than a Trinket? It's an Adafruit ItsyBitsy M4 Express featuring the Microchip ATSAMD51! Small, powerful, with a ultra fast ATSAMD51 Cortex M4 processor running at 120 MHz - this microcontroller board is perfect when you want something very compact, with a ton of horsepower and a bunch of pins. This Itsy is like a bullet train, with it's 120MHz Cortex M4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
